// Logisim project swap.circ as structural Verilog: 1 circuit, main circuit main
module main (
  input  W,
  input  Reset,
  output Done
);

  wire and_1_out, and_2_out, and_3_out, and_5_out, and_6_out, ck_out, controlled_buffer_1_out, d_ff_1_q,
       d_ff_1_qn, d_ff_2_q, d_ff_2_qn, or_1_out, or_2_out, R1_q, R2_q, R3_q;

  and and_1 (and_1_out, d_ff_2_q, d_ff_1_qn);
  and and_2 (and_2_out, d_ff_1_q, d_ff_2_qn);
  and and_3 (and_3_out, d_ff_2_qn, W);
  Clock ck (.out(ck_out));
  Register #(.width(1)) R1 (.D(controlled_buffer_1_out), .Q(R1_q), .clk(ck_out), .clr(Done));  // open: en
  Register #(.width(1)) R2 (.D(controlled_buffer_1_out), .Q(R2_q), .clk(ck_out), .clr(and_6_out));  // open: en
  Register #(.width(1)) R3 (.D(controlled_buffer_1_out), .Q(R3_q), .clk(ck_out), .clr(and_5_out));  // open: en
  or or_1 (or_1_out, and_1_out, and_2_out);
  or or_2 (or_2_out, and_2_out, and_3_out);
  assign controlled_buffer_1_out = and_6_out ? R1_q : 1'bz;  // Controlled_Buffer controlled_buffer_1
  assign controlled_buffer_1_out = and_5_out ? R2_q : 1'bz;  // Controlled_Buffer controlled_buffer_2
  assign controlled_buffer_1_out = Done ? R3_q : 1'bz;  // Controlled_Buffer controlled_buffer_3
  D_Flip_Flop d_ff_1 (.clk(ck_out), .D(or_1_out), .Q(d_ff_1_q), .Qn(d_ff_1_qn), .en(Reset));  // open: preset, reset
  D_Flip_Flop d_ff_2 (.clk(ck_out), .D(or_2_out), .Q(d_ff_2_q), .Qn(d_ff_2_qn), .en(Reset));  // open: preset, reset
  and and_4 (Done, d_ff_1_q, d_ff_2_q);
  and and_5 (and_5_out, d_ff_1_qn, d_ff_2_q);
  and and_6 (and_6_out, d_ff_1_q, d_ff_2_qn);

  // Notes on the sheet:
  //   C1
  //   H3
  //   H2
  //   C3
  //   H1
  //   C2
endmodule
